// Logisim project microcalcolatore.circ as structural Verilog: 1 circuit, main circuit Microcalc β2015
module \Microcalc_β2015  (
  input  [4:0] INPUT,
  output [4:0] OUTPUT,
  output out_3
);

  wire button_1_out, clock_out, not_1_out, not_2_out, not_3_out, or_1_out, or_2_out, or_3_out, RESET_out,
       t_ff_1_qn, \β2015_ioreq , \β2015_mreq , \β2015_read , \β2015_wr ;
  wire [4:0] \β2015_address , \β2015_data_out ;

  Clock clock (.out(clock_out));
  Button RESET (.out(RESET_out));
  \ß2015  \u_β2015  (
    .DATA_IN(\β2015_data_out ), .CLOCK(t_ff_1_qn), .WAIT(clock_out), .RESET(RESET_out),
    .ADDRESS(\β2015_address ), .MREQ(\β2015_mreq ), .READ(\β2015_read ), .IOREQ(\β2015_ioreq ),
    .WR(\β2015_wr ), .DATA_OUT(\β2015_data_out ));
  or or_1 (or_1_out, \β2015_mreq , \β2015_read );
  or or_2 (or_2_out, \β2015_wr , \β2015_ioreq );
  or or_3 (or_3_out, \β2015_ioreq , \β2015_read );
  not not_1 (not_1_out, or_1_out);
  ROM #(.addrWidth(5), .dataWidth(5)) rom_1 (.addr(\β2015_address ), .data(\β2015_data_out ), .sel(not_1_out));
  Register #(.width(5)) register_1 (.D(\β2015_data_out ), .Q(OUTPUT), .clk(or_2_out));  // open: en, clr
  not not_2 (not_2_out, or_3_out);
  Button button_1 (.out(button_1_out));
  T_Flip_Flop #(.Pre_Clr_Positions("LEGACY"), .enable("true"), .NewFFLayout("false")) t_ff_1 (
    .clk(not_2_out), .T(1'b1), .Q(out_3), .Qn(t_ff_1_qn), .reset(button_1_out));  // open: preset, en
  not not_3 (not_3_out, or_3_out);
  assign \β2015_data_out  = not_3_out ? INPUT : 5'bz;  // Controlled_Buffer controlled_buffer_1

  // Notes on the sheet:
  //   V 1.3
  //   contents of rom_1 (hex, n*v repeats v):
  //   c 4 1 0 6 4 c 5 1 0 3 5 1 0 7 a e e 8 b 16 0 d
endmodule
