// Logisim project Test moltiplicazioni (1).circ as structural Verilog: 1 circuit, main circuit esterno
module esterno (
  input  [4:0] in_1,
  input  RESET,
  output [4:0] out_3,
  output out_4
);

  wire button_1_out, clock_out, not_1_out, not_2_out, not_3_out, not_4_out, or_1_out, or_2_out, or_3_out,
       t_ff_1_qn, \ß2015_1_ioreq , \ß2015_1_mreq , \ß2015_1_read , \ß2015_1_wr ;
  wire [4:0] \ß2015_1_address , \ß2015_1_data_out ;

  Clock clock (.out(clock_out));
  \ß2015  \u_ß2015_1  (
    .DATA_IN(\ß2015_1_data_out ), .CLOCK(clock_out), .WAIT(t_ff_1_qn), .RESET(RESET),
    .ADDRESS(\ß2015_1_address ), .MREQ(\ß2015_1_mreq ), .READ(\ß2015_1_read ), .IOREQ(\ß2015_1_ioreq ),
    .WR(\ß2015_1_wr ), .DATA_OUT(\ß2015_1_data_out ));
  or or_1 (or_1_out, \ß2015_1_mreq , \ß2015_1_read );
  or or_2 (or_2_out, \ß2015_1_wr , \ß2015_1_ioreq );
  or or_3 (or_3_out, \ß2015_1_ioreq , \ß2015_1_read );
  not not_1 (not_1_out, or_1_out);
  ROM #(.addrWidth(5), .dataWidth(5)) rom_1 (.addr(\ß2015_1_address ), .data(\ß2015_1_data_out ), .sel(not_1_out));
  Register #(.width(5)) register_1 (.D(\ß2015_1_data_out ), .Q(out_3), .clk(or_2_out));  // open: en, clr
  Button button_1 (.out(button_1_out));
  not not_2 (not_2_out, or_3_out);
  not not_3 (not_3_out, \ß2015_1_ioreq );
  T_Flip_Flop #(.Pre_Clr_Positions("LEGACY"), .enable("true"), .NewFFLayout("false")) t_ff_1 (
    .clk(not_2_out), .T(1'b1), .Q(out_4), .Qn(t_ff_1_qn), .reset(button_1_out), .en(not_3_out));  // open: preset
  not not_4 (not_4_out, or_3_out);
  assign \ß2015_1_data_out  = not_4_out ? in_1 : 5'bz;  // Controlled_Buffer controlled_buffer_1

  // Notes on the sheet:
  //   contents of rom_1 (hex, n*v repeats v):
  //   c 4 1 0 6 4 c 5 1 0 3 5 1 0 7 a e e 8 b 16 0 d
endmodule
