// Logisim project Test moltiplicazioni.circ as structural Verilog: 1 circuit, main circuit esterno
module esterno (
  input  RESET,
  input  [4:0] in_2,
  output [4:0] out_3,
  output out_4
);

  wire and_1_out, and_2_out, button_1_out, clock_out, not_1_out, not_2_out, not_3_out, not_4_out, not_5_out,
       or_1_out, or_2_out, or_3_out, t_ff_1_qn, \ß2015_1_ioreq , \ß2015_1_mreq , \ß2015_1_ram_load ,
       \ß2015_1_read , \ß2015_1_wr ;
  wire [4:0] \ß2015_1_address , \ß2015_1_data_out ;

  Clock clock (.out(clock_out));
  \ß2015  \u_ß2015_1  (
    .DATA_IN(\ß2015_1_data_out ), .CLOCK(t_ff_1_qn), .WAIT(clock_out), .RESET(RESET),
    .ADDRESS(\ß2015_1_address ), .RAM_LOAD(\ß2015_1_ram_load ), .MREQ(\ß2015_1_mreq ), .READ(\ß2015_1_read ),
    .IOREQ(\ß2015_1_ioreq ), .WR(\ß2015_1_wr ), .DATA_OUT(\ß2015_1_data_out ));  // open: out_12
  or or_1 (or_1_out, \ß2015_1_mreq , \ß2015_1_read );
  or or_2 (or_2_out, \ß2015_1_wr , \ß2015_1_ioreq );
  or or_3 (or_3_out, \ß2015_1_ioreq , \ß2015_1_read );
  and and_1 (and_1_out, ~or_1_out, \ß2015_1_address [4]);  // AND_Gate
  not not_1 (not_1_out, \ß2015_1_address [4]);
  not not_2 (not_2_out, or_1_out);
  and and_2 (and_2_out, not_1_out, not_2_out);
  RAM #(.addrWidth(4), .dataWidth(5), .bus("asynch")) ram_1 (
    .addr(\ß2015_1_address [3:0]), .data(\ß2015_1_data_out ), .sel(and_1_out), .ld(not_3_out));  // open: clr
  not not_3 (not_3_out, \ß2015_1_ram_load );
  ROM #(.addrWidth(4), .dataWidth(5)) rom_1 (.addr(\ß2015_1_address [3:0]), .data(\ß2015_1_data_out ), .sel(and_2_out));
  Register #(.width(5)) register_1 (.D(\ß2015_1_data_out ), .Q(out_3), .clk(or_2_out));  // open: en, clr
  Button button_1 (.out(button_1_out));
  not not_4 (not_4_out, or_3_out);
  T_Flip_Flop #(.Pre_Clr_Positions("LEGACY"), .enable("true"), .NewFFLayout("false")) t_ff_1 (
    .clk(not_4_out), .T(1'b1), .Q(out_4), .Qn(t_ff_1_qn), .reset(button_1_out));  // open: preset, en
  not not_5 (not_5_out, or_3_out);
  assign \ß2015_1_data_out  = not_5_out ? in_2 : 5'bz;  // Controlled_Buffer controlled_buffer_1

  // Notes on the sheet:
  //   contents of rom_1 (hex, n*v repeats v):
  //   12 19 1 0 6 4 c 5 1 0 3 5 1 0 7 a
endmodule
