// Logisim project B2018.circ as structural Verilog: 4 circuits, main circuit ß2018
module \ß2018  (
  input  [7:0] DATA_IN,
  input  CLOCK,
  input  WAIT,
  input  RESET,
  output [7:0] ADDRESS,
  output MREQ,
  output READ,
  output IOREQ,
  output WR,
  output [7:0] DATA_OUT
);

  wire _0, _1, _3, _4, _5, _8, _9, _10, _11, _12, _13, _14, _15, _16, _17, _18, _19, _20, _22, _23, _24, _25,
       _26, _27, _28, _29, _30, _31, A, and_1_out, B, C, controlled_buffer_7_out, controlled_buffer_8_out,
       controlled_buffer_9_out, D, E, F, not_1_out, not_2_out, or_1_out, or_2_out, S1, S2, S3, S4, S4_t,
       Test_disabilita_altra_entrata_1___no__0___si, Test_out;
  wire [6:5] alu_1_z;
  wire [7:0] A_q, alu_1_result, ALUREG_q, B_q, C_q, controlled_buffer_1_out, D_q, data_register_q, FLAG_q,
       Instruction_Register_q, multiplexer_1_out, PCBackup_q, TEMP_q;

  Decoder #(.select(3), .enable("false")) decoder_1 (
    .out1(C), .out2(B), .out3(A), .out4(D), .out5(E), .out6(F), .sel({_27, _30, _31}));  // open: out0, out7
  LED BUS__TEMP (.in(_0));
  LED u_READ (.in(_16));
  Multiplexer #(.width(8), .enable("false")) multiplexer_1 (
    .in0(controlled_buffer_1_out), .in1({8{1'b1}}), .out(multiplexer_1_out), .sel(RESET));
  LED BUS__C (.in(S3));
  LED led_1 (.in(_1));
  LED u_WR (.in(_18));
  LED u_IOREQ (.in(_17));
  or or_1 (or_1_out, RESET, _14);
  Register #(.trigger("falling")) Instruction_Register (
    .D(multiplexer_1_out), .Q(Instruction_Register_q), .clk(or_2_out));  // open: en, clr
  or or_2 (or_2_out, RESET, _11);
  LED ALU0 (.in(_4));
  LED led_2 (.in(_3));
  LED ALU__REG (.in(_19));
  and and_1 (and_1_out, WAIT, CLOCK);
  LED PCBK (.in(_5));
  LED BUS__A (.in(S1));
  LED CP (.in(_20));
  LED BUS__D (.in(S4_t));
  LED ALU1 (.in(_8));
  LED BUS__Dout (.in(_22));
  LED BUS__B (.in(S2));
  LED C__BUS (.in(A));
  LED B__BUS (.in(B));
  Control_Unit Control_Unit (
    .Internal_clock(and_1_out), .Internal_reset(or_1_out), .Op_Code(Instruction_Register_q),
    .Control_Output({_31, _30, _29, _28, _27, _26, _25, _24, _23, _22, S2, _20, _19, _18, _17, _16, _15, _14, _13, _12, _11, _10, _9, _8, S4_t, S1, _5, _4, _3, S3, _1, _0}));  // open: CU_COUNTER
  Register u_A (.D(controlled_buffer_1_out), .Q(A_q), .clk(S1));  // open: en, clr
  assign controlled_buffer_1_out = A ? A_q : 8'bz;  // Controlled_Buffer controlled_buffer_1
  Register u_B (.D(controlled_buffer_1_out), .Q(B_q), .clk(S2));  // open: en, clr
  assign controlled_buffer_1_out = B ? B_q : 8'bz;  // Controlled_Buffer controlled_buffer_2
  Register u_C (.D(controlled_buffer_1_out), .Q(C_q), .clk(S3));  // open: en, clr
  assign controlled_buffer_1_out = C ? C_q : 8'bz;  // Controlled_Buffer controlled_buffer_3
  Register u_D (.D(controlled_buffer_1_out), .Q(D_q), .clk(S4));  // open: en, clr
  assign controlled_buffer_1_out = F ? D_q : 8'bz;  // Controlled_Buffer controlled_buffer_4
  LED PC_plus_plus (.in(_9));
  LED PC_COUNT (.in(_23));
  LED A__BUS (.in(C));
  ALU alu_1 (.OP1(A_q), .OP2(TEMP_q), .op({_26, _8, _4}), .S(alu_1_z[6]), .Z(alu_1_z[5]), .Result(alu_1_result));
  Register TEMP (.D(controlled_buffer_1_out), .Q(TEMP_q), .clk(_0));  // open: en, clr
  LED BUS__IR (.in(_11));
  LED LD_PC (.in(_10));
  LED CN (.in(_24));
  LED ALU__BUS (.in(D));
  assign controlled_buffer_1_out = E ? data_register_q : 8'bz;  // Controlled_Buffer controlled_buffer_5
  Register #(.trigger("falling")) data_register (.D(DATA_IN), .Q(data_register_q), .clk(_12));  // open: en, clr
  assign controlled_buffer_1_out = D ? ALUREG_q : 8'bz;  // Controlled_Buffer controlled_buffer_6
  Register ALUREG (.D(alu_1_result), .Q(ALUREG_q), .clk(_19));  // open: en, clr
  Register FLAG (.D({1'b0, alu_1_z, {5{1'b0}}}), .Q(FLAG_q), .clk(_25));  // open: en, clr
  LED Din__DR (.in(_12));
  LED Flag_2 (.in(_25));
  LED ALU2 (.in(_26));
  LED DR__BUS (.in(E));
  LED CU_RESET (.in(_14));
  LED led_3 (.in(_13));
  LED DEC2 (.in(_27));
  LED D__BUS (.in(F));
  Test Test (
    .S(FLAG_q[6]), .Z(FLAG_q[5]), .out(Test_out),
    .disabilita_altra_entrata_1___no__0___si(Test_disabilita_altra_entrata_1___no__0___si), .not_eq(_29),
    .eq(_28), .pos(_20), .neg(_24));
  assign controlled_buffer_7_out = Test_disabilita_altra_entrata_1___no__0___si ? _10 : 1'bz;  // Controlled_Buffer controlled_buffer_7
  assign controlled_buffer_8_out = Test_disabilita_altra_entrata_1___no__0___si ? _23 : 1'bz;  // Controlled_Buffer controlled_buffer_8
  LED u_MREQ (.in(_15));
  LED CNZ (.in(_29));
  LED CZ (.in(_28));
  not not_1 (not_1_out, Test_disabilita_altra_entrata_1___no__0___si);
  assign controlled_buffer_9_out = not_1_out ? Test_out : 1'bz;  // Controlled_Buffer controlled_buffer_9
  Counter #(.behavior("old")) Program_Counter (
    .load(controlled_buffer_7_out), .D(controlled_buffer_1_out), .count(controlled_buffer_8_out),
    .Q(ADDRESS), .clk(_9), .clr(RESET));  // open: carry, preset
  LED DEC1 (.in(_30));
  assign controlled_buffer_7_out = not_1_out ? Test_out : 1'bz;  // Controlled_Buffer controlled_buffer_10
  not not_2 (not_2_out, controlled_buffer_9_out);
  assign controlled_buffer_8_out = not_1_out ? not_2_out : 1'bz;  // Controlled_Buffer controlled_buffer_11
  LED DEC0 (.in(_31));
  Register PCBackup (.D(ADDRESS), .Q(PCBackup_q), .clk(_5));  // open: en, clr
  assign controlled_buffer_1_out = _3 ? PCBackup_q : 8'bz;  // Controlled_Buffer controlled_buffer_12
  assign DATA_OUT = _22 ? controlled_buffer_1_out : 8'bz;  // Controlled_Buffer controlled_buffer_13
  not not_3 (MREQ, _15);
  not not_4 (READ, _16);
  not not_5 (IOREQ, _17);
  not not_6 (WR, _18);

  // Notes on the sheet:
  //   β2018 - V. 3.2 Dinapoli e Ontano
  //   Internal Data Bus
endmodule

module Control_Unit (
  input  Internal_clock,
  input  Internal_reset,
  input  [7:0] Op_Code,
  output [3:0] CU_COUNTER,
  output [31:0] Control_Output
);

  Counter #(.width(4), .max('hf), .behavior("old")) counter_1 (
    .Q(CU_COUNTER), .clk(Internal_clock), .clr(Internal_reset));  // open: load, D, count, carry, preset
  ROM #(.addrWidth(12), .dataWidth(32), .Select("high")) rom_1 (.addr({Op_Code, CU_COUNTER}), .data(Control_Output));

  // Notes on the sheet:
  //   contents of rom_1 (hex, n*v repeats v):
  //   800000 800200 19000 88000800 88004000 59*0 40000000 40000101 a080100 8200000 800000 800200 19000
  //   88000800 88004000 7*0 40000000 40000111 a080110 8200000 800000 800200 19000 88000800 88004000 7*0
  //   819000 819200 88000000 88200000 800000 800200 19000 88000800 88004000 87*0 2 103 a080100 8000004
  //   800000 800200 19000 88000800 88004000 7*0 2 113 a080110 8000004 800000 800200 19000 88000800
  //   88004000 7*0 819000 819200 88000000 88000004 800000 800200 19000 88000800 88004000 23*0 11111111
  //   15*0 11111111 15*0 11111111 15*0 11111111 15*0 48000000 48000101 a080100 8000080 800000 800200 19000
  //   88000800 88004000 7*0 48000000 48000111 a080110 8000080 800000 800200 19000 88000800 88004000 7*0
  //   819000 819200 88000000 88000080 800000 800200 19000 88000800 88004000 599*0 c0000000 c0000101
  //   a080100 8000040 800000 800200 19000 88000800 88004000 7*0 c0000000 c0000111 a080110 8000040 800000
  //   800200 19000 88000800 88004000 7*0 819000 819200 88000000 88000040 800000 800200 19000 88000800
  //   88004000 39*0 80000000 80200000 800000 800200 19000 88000800 88004000 9*0 48000000 48200000 800000
  //   800200 19000 88000800 88004000 73*0 c0000000 c0200000 800000 800200 19000 88000800 88004000 9*0
  //   40000000 40000004 800000 800200 19000 88000800 88004000 25*0 48000000 48000004 800000 800200 19000
  //   88000800 88004000 73*0 c0000000 c0000004 800000 800200 19000 88000800 88004000 9*0 40000000 40000080
  //   800000 800200 19000 88000800 88004000 9*0 80000000 80000080 800000 800200 19000 88000800 88004000
  //   89*0 c0000000 c0000080 800000 800200 19000 88000800 88004000 489*0 4000 31*0 40000000 40000040
  //   800000 800200 19000 88000800 88004000 9*0 80000000 80000040 800000 800200 19000 88000800 88004000
  //   9*0 48000000 48000040 800000 800200 19000 88000800 88004000 89*0 40000000 40000001 a080000 8000040
  //   800000 800200 19000 88000800 88004000 7*0 80000000 80000001 a080000 8000040 800000 800200 19000
  //   88000800 88004000 7*0 48000000 48000001 a080000 8000040 800000 800200 19000 88000800 88004000 215*0
  //   40000000 40000011 a080010 8000040 800000 800200 19000 88000800 88004000 7*0 80000000 80000011
  //   a080010 8000040 800000 800200 19000 88000800 88004000 7*0 48000000 48000011 a080010 8000040 800000
  //   800200 19000 88000800 88004000 759*0 800000 800200 88019000 88000000 a8019000 a8019200 88000800
  //   88004000 8*0 800000 800200 88019000 88000000 88000400 88019600 88000800 88004000 40*0 819000 819200
  //   88000000 88000001 a080000 8000040 800000 800200 19000 88000800 88004000 53*0 800000 800200 88019000
  //   88000000 98019000 98019200 88000800 88004000 136*0 819000 819200 20 88000400 200 c0400000 c0460000
  //   408 800200 800000 800200 19000 88000800 88004000 34*0 819000 819200 88000000 88000011 a080010
  //   8000040 800000 800200 19000 88000800 88004000 69*0 30000 31000 30000 20 88000400 31200 30000 408
  //   88000600 88000040 800200 800000 800200 19000 88000800 88004000 160*0 819000 819200 88000000 8c000011
  //   e080010 8000040 800000 800200 19000 88000800 88004000 117*0 819000 819200 88000000 8c000001 e080000
  //   8000040 800000 800200 19000 88000800 88004000 53*0 800000 800200 88019000 88000000 88119000 88119200
  //   88000800 88004000 56*0 819000 819200 88000000 8c000101 e080100 8000040 800000 800200 19000 88000800
  //   88004000 53*0 800000 800200 88019000 88000000 89059000 89059200 88000800 88004000 56*0 819000 819200
  //   88000000 88000001 10 2000000 800000 800200 19000 88000800 88004000 5*0 19000 88018800 8801c000
endmodule

module ALU (
  input  [7:0] OP1,
  input  [7:0] OP2,
  input  [2:0] op,
  output [7:0] Result,
  output S,
  output Z
);

  wire decoder_1_out0, decoder_1_out1, decoder_1_out2, decoder_1_out3, decoder_1_out4, decoder_1_out5,
       decoder_1_out6;
  wire [7:0] adder_1_out, adder_2_out, and_1_out, or_1_out, subtractor_1_out, subtractor_2_out, xor_1_out;

  Decoder #(.select(3)) decoder_1 (
    .out0(decoder_1_out0), .out1(decoder_1_out1), .out2(decoder_1_out2), .out3(decoder_1_out3),
    .out4(decoder_1_out4), .out5(decoder_1_out5), .out6(decoder_1_out6), .sel(op));  // open: out7, en
  assign or_1_out = OP2 | OP1;  // OR_Gate or_1, 8 bits wide
  assign and_1_out = OP2 & OP1;  // AND_Gate and_1, 8 bits wide
  assign xor_1_out = OP2 ^ OP1;  // XOR_Gate xor_1, 8 bits wide
  Adder adder_1 (.a(OP1), .b(OP2), .out(adder_1_out));  // open: cin, cout
  Subtractor subtractor_1 (.a(OP1), .b(OP2), .out(subtractor_1_out));  // open: bin, bout
  Adder adder_2 (.a(OP2), .b(8'h1), .out(adder_2_out));  // open: cin, cout
  Subtractor subtractor_2 (.a(OP2), .b(8'h1), .out(subtractor_2_out));  // open: bin, bout
  assign Result = decoder_1_out0 ? adder_1_out : 8'bz;  // Controlled_Buffer controlled_buffer_1
  assign Result = decoder_1_out1 ? subtractor_1_out : 8'bz;  // Controlled_Buffer controlled_buffer_2
  assign Result = decoder_1_out2 ? adder_2_out : 8'bz;  // Controlled_Buffer controlled_buffer_3
  assign Result = decoder_1_out3 ? subtractor_2_out : 8'bz;  // Controlled_Buffer controlled_buffer_4
  assign Result = decoder_1_out5 ? and_1_out : 8'bz;  // Controlled_Buffer controlled_buffer_5
  assign Result = decoder_1_out4 ? xor_1_out : 8'bz;  // Controlled_Buffer controlled_buffer_6
  assign Result = decoder_1_out6 ? or_1_out : 8'bz;  // Controlled_Buffer controlled_buffer_7
  Comparator comparator_1 (.a(Result), .b({8{1'b0}}), .eq(Z));  // open: gt, lt

  assign S = Result[7];

  // Notes on the sheet:
  //   000 somma - 001 sottrazione - 010 inc - 011 dec - 100 xor - 101 and - 110 or
endmodule

module Test (
  input  S,
  input  Z,
  input  not_eq,
  input  eq,
  input  pos,
  input  neg,
  output disabilita_altra_entrata_1___no__0___si,
  output out
);

  wire comparator_1_eq, comparator_2_eq, comparator_3_eq, comparator_4_eq;

  Comparator #(.width(1)) comparator_1 (.a(S), .b(1'b1), .eq(comparator_1_eq));  // open: gt, lt
  assign out = neg ? comparator_1_eq : 1'bz;  // Controlled_Buffer controlled_buffer_1
  Comparator #(.width(1)) comparator_2 (.a(S), .b(1'b0), .eq(comparator_2_eq));  // open: gt, lt
  assign out = pos ? comparator_2_eq : 1'bz;  // Controlled_Buffer controlled_buffer_2
  assign out = eq ? comparator_4_eq : 1'bz;  // Controlled_Buffer controlled_buffer_3
  Comparator #(.width(1)) comparator_3 (.a(Z), .b(1'b0), .eq(comparator_3_eq));  // open: gt, lt
  Comparator #(.width(1)) comparator_4 (.a(Z), .b(1'b1), .eq(comparator_4_eq));  // open: gt, lt
  assign out = not_eq ? comparator_3_eq : 1'bz;  // Controlled_Buffer controlled_buffer_4
  nor nor_1 (disabilita_altra_entrata_1___no__0___si, not_eq, pos, eq, neg);
endmodule
