// Logisim project microprocessore8bitconTunnel.circ as structural Verilog: 4 circuits, main circuit Control Unit
module Control_Unit (
  input  Internal_clock,
  input  Reset,
  input  [7:0] Op_Code,
  output [3:0] CU_COUNTER,
  output [31:0] Control_Output
);

  Counter #(.width(4), .max('hf)) counter_1 (
    .Q(CU_COUNTER), .clk(Internal_clock), .clr(Reset));  // open: load, D, count, carry
  ROM #(.addrWidth(12), .dataWidth(32)) rom_1 (.addr({Op_Code, CU_COUNTER}), .data(Control_Output));  // open: sel

  // Notes on the sheet:
  //   contents of rom_1 (hex, n*v repeats v):
  //   61000 62800 66000 13*70000 821000 821200 22000 22040 821000 821200 20000 22800 26000 7*70000 20008
  //   20048 821000 821200 20000 22800 26000 9*70000 20002 20042 821000 821200 20000 22800 26000 9*70000
  //   60020 260020 861000 861200 60000 62800 66000 9*70000 60020 60024 861000 861200 60000 62800 66000
  //   9*70000 20008 20009 a0080 200c0 821000 821200 20000 22800 26000 7*70000 20002 20003 a0080 200c0
  //   821000 821200 20000 22800 26000 7*70000 20002 20013 a0090 200c0 821000 821200 20000 22800 26000
  //   7*70000 20008 20109 a0180 220080 821000 821200 20000 22800 26000 7*70000 20008 20119 a0190 220080
  //   821000 821200 20000 22800 26000 7*70000 820000 820200 23000 22000 23400 23600 20000 22800 26000
  //   7*70000 48000 49000 48000 62000 62040 861000 861200 60000 62800 66000 6*70000 410020 470020 821000
  //   821200 20000 22800 26000 9*70000 820000 820200 23000 22000 123000 123200 20000 22800 26000 7*70000
  //   820000 820200 23000 22000 1023000 1023200 20000 22800 26000 7*70000
endmodule

module GP2015 (
  input  [7:0] DATA,
  input  WAIT,
  input  CLOCK,
  input  RESET,
  output [3:0] CU_COUNTER,
  output [7:0] Address,
  output MREQ,
  output READ,
  output IOREQ,
  output WR,
  output [7:0] DATA_OUT
);

  wire alu_1_flag, ALU_OP_1, ALU_OP_2, ALU_READ, and_1_out, CLK_A, CLK_B, CLK_C, controlled_buffer_6_out,
       controlled_buffer_7_out, controlled_buffer_8_out, controllo_1_disabilita_altra_entrata_1___no__0___si,
       controllo_1_out, CONTROLLO_NEGATIVO, CONTROLLO_POSITIVO, COUNT_PC, CU_RESET, DATA_REG_CLK,
       DATA_REG_LD, FLAG_q, INST_REG_CLK, LD_A, LD_ALU, LD_B, LD_C, LD_PC, not_1_out, not_2_out, OUT_DATA,
       PC_CLOCK, Tmp_Clock;
  wire [7:0] A_q, alu_1_result, ALUREG_q, B_q, C_q, controlled_buffer_1_out, data_register_q,
       Instruction_Register_q, TEMP_q;
  wire [31:25] TUNNEL;

  Register #(.trigger("falling")) Instruction_Register (
    .D(controlled_buffer_1_out), .Q(Instruction_Register_q), .clk(INST_REG_CLK), .clr(RESET));  // open: en
  and and_1 (and_1_out, WAIT, CLOCK);
  Control_Unit control_unit_1 (
    .Internal_clock(and_1_out), .Reset(CU_RESET), .Op_Code(Instruction_Register_q), .CU_COUNTER(CU_COUNTER),
    .Control_Output({TUNNEL, CONTROLLO_NEGATIVO, COUNT_PC, OUT_DATA, CLK_B, CONTROLLO_POSITIVO, ALU_READ, WR, IOREQ, READ, MREQ, CU_RESET, DATA_REG_LD, DATA_REG_CLK, INST_REG_CLK, LD_PC, PC_CLOCK, ALU_OP_2, LD_ALU, CLK_A, LD_A, ALU_OP_1, LD_B, CLK_C, LD_C, Tmp_Clock}));
  Register A (.D(controlled_buffer_1_out), .Q(A_q), .clk(CLK_A));  // open: en, clr
  assign controlled_buffer_1_out = LD_B ? B_q : 8'bz;  // Controlled_Buffer controlled_buffer_1
  Register B (.D(controlled_buffer_1_out), .Q(B_q), .clk(CLK_B));  // open: en, clr
  Register C (.D(controlled_buffer_1_out), .Q(C_q), .clk(CLK_C));  // open: en, clr
  assign controlled_buffer_1_out = LD_A ? A_q : 8'bz;  // Controlled_Buffer controlled_buffer_2
  assign controlled_buffer_1_out = LD_C ? C_q : 8'bz;  // Controlled_Buffer controlled_buffer_3
  ALU alu_1 (.OP1(A_q), .OP2(TEMP_q), .op({ALU_OP_2, ALU_OP_1}), .Flag(alu_1_flag), .Result(alu_1_result));
  Register TEMP (.D(controlled_buffer_1_out), .Q(TEMP_q), .clk(Tmp_Clock));  // open: en, clr
  Register #(.trigger("falling")) data_register (.D(DATA), .Q(data_register_q), .clk(DATA_REG_CLK));  // open: en, clr
  assign controlled_buffer_1_out = DATA_REG_LD ? data_register_q : 8'bz;  // Controlled_Buffer controlled_buffer_4
  Register ALUREG (.D(alu_1_result), .Q(ALUREG_q), .clk(ALU_READ));  // open: en, clr
  assign controlled_buffer_1_out = LD_ALU ? ALUREG_q : 8'bz;  // Controlled_Buffer controlled_buffer_5
  Register #(.width(1)) FLAG (.D(alu_1_flag), .Q(FLAG_q), .clk(ALU_READ));  // open: en, clr
  controllo controllo_1 (
    .Flag(FLAG_q), .out(controllo_1_out),
    .disabilita_altra_entrata_1___no__0___si(controllo_1_disabilita_altra_entrata_1___no__0___si),
    .pos(CONTROLLO_POSITIVO), .neg(CONTROLLO_NEGATIVO));
  assign controlled_buffer_6_out = controllo_1_disabilita_altra_entrata_1___no__0___si ? LD_PC : 1'bz;  // Controlled_Buffer controlled_buffer_6
  assign controlled_buffer_7_out = controllo_1_disabilita_altra_entrata_1___no__0___si ? COUNT_PC : 1'bz;  // Controlled_Buffer controlled_buffer_7
  not not_1 (not_1_out, controllo_1_disabilita_altra_entrata_1___no__0___si);
  assign controlled_buffer_8_out = not_1_out ? controllo_1_out : 1'bz;  // Controlled_Buffer controlled_buffer_8
  Counter Program_Counter (
    .load(controlled_buffer_6_out), .D(controlled_buffer_1_out), .count(controlled_buffer_7_out),
    .Q(Address), .clk(PC_CLOCK), .clr(RESET));  // open: carry
  assign controlled_buffer_6_out = not_1_out ? controllo_1_out : 1'bz;  // Controlled_Buffer controlled_buffer_9
  not not_2 (not_2_out, controlled_buffer_8_out);
  assign controlled_buffer_7_out = not_1_out ? not_2_out : 1'bz;  // Controlled_Buffer controlled_buffer_10
  assign DATA_OUT = OUT_DATA ? controlled_buffer_1_out : 8'bz;  // Controlled_Buffer controlled_buffer_11

  // Other names for the same wires on the sheet: TUNNEL[24:0] = {CONTROLLO_NEGATIVO, COUNT_PC, OUT_DATA, CLK_B, CONTROLLO_POSITIVO, ALU_READ, WR, IOREQ, READ, MREQ, CU_RESET, DATA_REG_LD, DATA_REG_CLK, INST_REG_CLK, LD_PC, PC_CLOCK, ALU_OP_2, LD_ALU, CLK_A, LD_A, ALU_OP_1, LD_B, CLK_C, LD_C, Tmp_Clock}

  // Notes on the sheet:
  //   mettere instruction reg e data reg in falling edge
endmodule

module ALU (
  input  [7:0] OP1,
  input  [7:0] OP2,
  input  [1:0] op,
  output [7:0] Result,
  output Flag
);

  wire decoder_1_out0, decoder_1_out1, decoder_1_out2, decoder_1_out3;
  wire [7:0] adder_1_out, adder_2_out, subtractor_1_out, subtractor_2_out;

  Decoder #(.select(2)) decoder_1 (
    .out0(decoder_1_out0), .out1(decoder_1_out1), .out2(decoder_1_out2), .out3(decoder_1_out3), .sel(op));  // open: en
  assign {Flag, Result[6:0]} = decoder_1_out0 ? adder_1_out : 8'bz;  // Controlled_Buffer controlled_buffer_1
  Adder adder_1 (.a(OP1), .b(OP2), .out(adder_1_out));  // open: cin, cout
  Subtractor subtractor_1 (.a(OP1), .b(OP2), .out(subtractor_1_out));  // open: bin, bout
  assign {Flag, Result[6:0]} = decoder_1_out1 ? subtractor_1_out : 8'bz;  // Controlled_Buffer controlled_buffer_2
  Adder adder_2 (.a(OP2), .b(8'h1), .out(adder_2_out));  // open: cin, cout
  Subtractor subtractor_2 (.a(OP2), .b(8'h1), .out(subtractor_2_out));  // open: bin, bout
  assign {Flag, Result[6:0]} = decoder_1_out2 ? adder_2_out : 8'bz;  // Controlled_Buffer controlled_buffer_3
  assign {Flag, Result[6:0]} = decoder_1_out3 ? subtractor_2_out : 8'bz;  // Controlled_Buffer controlled_buffer_4

  assign Result[7] = Flag;

  // Notes on the sheet:
  //   00 somma - 01 sottrazione - 10 inc - 11 dec
endmodule

module controllo (
  input  Flag,
  input  pos,
  input  neg,
  output disabilita_altra_entrata_1___no__0___si,
  output out
);

  wire comparator_1_eq, comparator_2_eq;

  Comparator #(.width(1)) comparator_1 (.a(Flag), .b(1'b1), .eq(comparator_1_eq));  // open: gt, lt
  assign out = neg ? comparator_1_eq : 1'bz;  // Controlled_Buffer controlled_buffer_1
  Comparator #(.width(1)) comparator_2 (.a(Flag), .b(1'b0), .eq(comparator_2_eq));  // open: gt, lt
  assign out = pos ? comparator_2_eq : 1'bz;  // Controlled_Buffer controlled_buffer_2
  nor nor_1 (disabilita_altra_entrata_1___no__0___si, pos, neg);
endmodule
