// Logisim project ß2017+Microcontrollore.circ as structural Verilog: 5 circuits, main circuit Control Unit
module Control_Unit (
  input  Internal_clock,
  input  Reset,
  input  [3:0] Op_Code,
  output [3:0] CU_COUNTER,
  output [24:0] Control_Output
);

  Counter #(.width(4), .max('hf)) counter_1 (
    .Q(CU_COUNTER), .clk(Internal_clock), .clr(Reset));  // open: load, D, count, carry
  ROM #(.dataWidth(25)) rom_1 (.addr({Op_Code, CU_COUNTER}), .data(Control_Output));  // open: sel

  // Notes on the sheet:
  //   contents of rom_1 (hex, n*v repeats v):
  //   21000 22800 26000 13*0 821000 821200 22000 22040 821000 821200 20000 22800 26000 7*0 20008 20048
  //   821000 821200 20000 22800 26000 9*0 20002 20042 821000 821200 20000 22800 26000 9*0 20020 220020
  //   821000 821200 20000 22800 26000 9*0 20020 20024 821000 821200 20000 22800 26000 9*0 20008 20009
  //   a0080 200c0 821000 821200 20000 22800 26000 7*0 20002 20003 a0080 200c0 821000 821200 20000 22800
  //   26000 7*0 20002 20013 a0090 200c0 821000 821200 20000 22800 26000 7*0 20008 20109 a0180 220080
  //   821000 821200 20000 22800 26000 7*0 20008 20119 a0190 220080 821000 821200 20000 22800 26000 7*0
  //   820000 820200 23000 22000 23400 23600 20000 22800 26000 7*0 48000 49000 48000 22000 22040 821000
  //   821200 20000 22800 26000 6*0 410020 470020 821000 821200 20000 22800 26000 9*0 820000 820200 23000
  //   22000 123000 123200 20000 22800 26000 7*0 820000 820200 23000 22000 1023000 1023200 20000 22800
  //   26000
endmodule

module GP2015 (
  input  [3:0] DATA,
  input  WAIT,
  input  CLOCK,
  input  RESET,
  output [3:0] CU_COUNTER,
  output [3:0] Address,
  output MREQ,
  output READ,
  output IOREQ,
  output WR,
  output [3:0] DATA_OUT
);

  wire alu_1_flag, and_1_out, controlled_buffer_6_out, controlled_buffer_7_out, controlled_buffer_8_out,
       controllo_1_disabilita_altra_entrata_1___no__0___si, controllo_1_out, FLAG_q, not_1_out, not_2_out;
  wire [3:0] A_q, alu_1_result, ALUREG_q, B_q, C_q, controlled_buffer_1_out, data_register_q,
       Instruction_Register_q, TEMP_q;
  wire [24:0] control_unit_1_control_output;

  Register #(.width(4), .trigger("falling")) Instruction_Register (
    .D(controlled_buffer_1_out), .Q(Instruction_Register_q), .clk(control_unit_1_control_output[11]),
    .clr(RESET));  // open: en
  and and_1 (and_1_out, WAIT, CLOCK);
  Control_Unit control_unit_1 (
    .Internal_clock(and_1_out), .Reset(control_unit_1_control_output[14]), .Op_Code(Instruction_Register_q),
    .CU_COUNTER(CU_COUNTER),
    .Control_Output({control_unit_1_control_output[24:19], WR, IOREQ, READ, MREQ, control_unit_1_control_output[14:0]}));
  Register #(.width(4)) A (
    .D(controlled_buffer_1_out), .Q(A_q), .clk(control_unit_1_control_output[6]));  // open: en, clr
  assign controlled_buffer_1_out = control_unit_1_control_output[3] ? B_q : 4'bz;  // Controlled_Buffer controlled_buffer_1
  Register #(.width(4)) B (
    .D(controlled_buffer_1_out), .Q(B_q), .clk(control_unit_1_control_output[21]));  // open: en, clr
  Register #(.width(4)) C (
    .D(controlled_buffer_1_out), .Q(C_q), .clk(control_unit_1_control_output[2]));  // open: en, clr
  assign controlled_buffer_1_out = control_unit_1_control_output[1] ? C_q : 4'bz;  // Controlled_Buffer controlled_buffer_2
  assign controlled_buffer_1_out = control_unit_1_control_output[5] ? A_q : 4'bz;  // Controlled_Buffer controlled_buffer_3
  ALU alu_1 (
    .OP1(A_q), .OP2(TEMP_q), .op({control_unit_1_control_output[8], control_unit_1_control_output[4]}),
    .Flag(alu_1_flag), .Result(alu_1_result));
  Register #(.width(4)) TEMP (
    .D(controlled_buffer_1_out), .Q(TEMP_q), .clk(control_unit_1_control_output[0]));  // open: en, clr
  assign controlled_buffer_1_out = control_unit_1_control_output[13] ? data_register_q : 4'bz;  // Controlled_Buffer controlled_buffer_4
  Register #(.width(4), .trigger("falling")) data_register (
    .D(DATA), .Q(data_register_q), .clk(control_unit_1_control_output[12]));  // open: en, clr
  Register #(.width(4)) ALUREG (
    .D(alu_1_result), .Q(ALUREG_q), .clk(control_unit_1_control_output[19]));  // open: en, clr
  assign controlled_buffer_1_out = control_unit_1_control_output[7] ? ALUREG_q : 4'bz;  // Controlled_Buffer controlled_buffer_5
  Register #(.width(1)) FLAG (.D(alu_1_flag), .Q(FLAG_q), .clk(control_unit_1_control_output[19]));  // open: en, clr
  controllo controllo_1 (
    .Flag(FLAG_q), .out(controllo_1_out),
    .disabilita_altra_entrata_1___no__0___si(controllo_1_disabilita_altra_entrata_1___no__0___si),
    .pos(control_unit_1_control_output[20]), .neg(control_unit_1_control_output[24]));
  assign controlled_buffer_6_out = controllo_1_disabilita_altra_entrata_1___no__0___si ? control_unit_1_control_output[10] : 1'bz;  // Controlled_Buffer controlled_buffer_6
  assign controlled_buffer_7_out = controllo_1_disabilita_altra_entrata_1___no__0___si ? control_unit_1_control_output[23] : 1'bz;  // Controlled_Buffer controlled_buffer_7
  not not_1 (not_1_out, controllo_1_disabilita_altra_entrata_1___no__0___si);
  assign controlled_buffer_8_out = not_1_out ? controllo_1_out : 1'bz;  // Controlled_Buffer controlled_buffer_8
  Counter #(.width(4), .max('hf)) Program_Counter (
    .load(controlled_buffer_6_out), .D(controlled_buffer_1_out), .count(controlled_buffer_7_out),
    .Q(Address), .clk(control_unit_1_control_output[9]), .clr(RESET));  // open: carry
  assign controlled_buffer_6_out = not_1_out ? controllo_1_out : 1'bz;  // Controlled_Buffer controlled_buffer_9
  not not_2 (not_2_out, controlled_buffer_8_out);
  assign controlled_buffer_7_out = not_1_out ? not_2_out : 1'bz;  // Controlled_Buffer controlled_buffer_10
  assign DATA_OUT = control_unit_1_control_output[22] ? controlled_buffer_1_out : 4'bz;  // Controlled_Buffer controlled_buffer_11

  // Notes on the sheet:
  //   mettere instruction reg e data reg in falling edge
endmodule

module ALU (
  input  [3:0] OP1,
  input  [3:0] OP2,
  input  [1:0] op,
  output [3:0] Result,
  output Flag
);

  wire decoder_1_out0, decoder_1_out1, decoder_1_out2, decoder_1_out3;
  wire [3:0] adder_1_out, adder_2_out, subtractor_1_out, subtractor_2_out;

  Decoder #(.select(2)) decoder_1 (
    .out0(decoder_1_out0), .out1(decoder_1_out1), .out2(decoder_1_out2), .out3(decoder_1_out3), .sel(op));  // open: en
  Adder #(.width(4)) adder_1 (.a(OP1), .b(OP2), .out(adder_1_out));  // open: cin, cout
  assign {Flag, Result[2:0]} = decoder_1_out0 ? adder_1_out : 4'bz;  // Controlled_Buffer controlled_buffer_1
  Subtractor #(.width(4)) subtractor_1 (.a(OP1), .b(OP2), .out(subtractor_1_out));  // open: bin, bout
  assign {Flag, Result[2:0]} = decoder_1_out1 ? subtractor_1_out : 4'bz;  // Controlled_Buffer controlled_buffer_2
  Adder #(.width(4)) adder_2 (.a(OP2), .b(4'b0001), .out(adder_2_out));  // open: cin, cout
  Subtractor #(.width(4)) subtractor_2 (.a(OP2), .b(4'b0001), .out(subtractor_2_out));  // open: bin, bout
  assign {Flag, Result[2:0]} = decoder_1_out2 ? adder_2_out : 4'bz;  // Controlled_Buffer controlled_buffer_3
  assign {Flag, Result[2:0]} = decoder_1_out3 ? subtractor_2_out : 4'bz;  // Controlled_Buffer controlled_buffer_4

  assign Result[3] = Flag;

  // Notes on the sheet:
  //   00 somma - 01 sottrazione - 10 inc - 11 dec
endmodule

module esterno (
  input  RESET,
  input  [3:0] in_2,
  output [3:0] CU_COUNTER,
  output out_4
);

  wire button_1_out, clock_out, gp2015_1_ioreq, gp2015_1_mreq, gp2015_1_read, gp2015_1_wr, not_1_out,
       not_2_out, not_3_out, or_1_out, or_2_out, or_3_out, t_ff_1_qn;
  wire [3:0] gp2015_1_address, gp2015_1_data_out, register_1_q;

  Clock clock (.out(clock_out));
  GP2015 gp2015_1 (
    .DATA(gp2015_1_data_out), .WAIT(t_ff_1_qn), .CLOCK(clock_out), .RESET(RESET), .CU_COUNTER(CU_COUNTER),
    .Address(gp2015_1_address), .MREQ(gp2015_1_mreq), .READ(gp2015_1_read), .IOREQ(gp2015_1_ioreq),
    .WR(gp2015_1_wr), .DATA_OUT(gp2015_1_data_out));
  or or_1 (or_1_out, gp2015_1_mreq, gp2015_1_read);
  or or_2 (or_2_out, gp2015_1_wr, gp2015_1_ioreq);
  or or_3 (or_3_out, gp2015_1_ioreq, gp2015_1_read);
  not not_1 (not_1_out, or_1_out);
  ROM #(.addrWidth(4), .dataWidth(4)) rom_1 (.addr(gp2015_1_address), .data(gp2015_1_data_out), .sel(not_1_out));
  Hex_Digit_Display hex_digit_display_1 (.value(register_1_q));  // open: dp
  Register #(.width(4)) register_1 (.D(gp2015_1_data_out), .Q(register_1_q), .clk(or_2_out));  // open: en, clr
  Button button_1 (.out(button_1_out));
  not not_2 (not_2_out, or_3_out);
  T_Flip_Flop t_ff_1 (.clk(not_2_out), .T(1'b1), .Q(out_4), .Qn(t_ff_1_qn), .reset(button_1_out));  // open: preset, en
  not not_3 (not_3_out, or_3_out);
  assign gp2015_1_data_out = not_3_out ? in_2 : 4'bz;  // Controlled_Buffer controlled_buffer_1

  // Notes on the sheet:
  //   contents of rom_1 (hex, n*v repeats v):
  //   c 4 c 5 1 0 7 a e 6 d
endmodule

module controllo (
  input  Flag,
  input  pos,
  input  neg,
  output disabilita_altra_entrata_1___no__0___si,
  output out
);

  wire comparator_1_eq, comparator_2_eq;

  Comparator #(.width(1)) comparator_1 (.a(Flag), .b(1'b1), .eq(comparator_1_eq));  // open: gt, lt
  assign out = neg ? comparator_1_eq : 1'bz;  // Controlled_Buffer controlled_buffer_1
  Comparator #(.width(1)) comparator_2 (.a(Flag), .b(1'b0), .eq(comparator_2_eq));  // open: gt, lt
  assign out = pos ? comparator_2_eq : 1'bz;  // Controlled_Buffer controlled_buffer_2
  nor nor_1 (disabilita_altra_entrata_1___no__0___si, pos, neg);
endmodule
